# Fritzing sketch Fritzing Model - LED Heart Module (saved by Fritzing 0.9.3b)
breadboards: 1

parts:
  Port_D2_=_LED1_Port_D11_=_LED10 = Arduino Uno (Rev3)
  LED1 = LED - 5mm [color="Red (633nm)" package="5 mm [THT]"]
  LED10 = LED - 5mm [color="Red (633nm)" package="5 mm [THT]"]
  LED2 = LED - 5mm [color="Red (633nm)" package="5 mm [THT]"]
  LED9 = LED - 5mm [color="Red (633nm)" package="5 mm [THT]"]
  LED8 = LED - 5mm [color="Red (633nm)" package="5 mm [THT]"]
  LED7 = LED - 5mm [color="Red (633nm)" package="5 mm [THT]"]
  LED_6 = LED - 5mm [color="Red (633nm)" package="5 mm [THT]"]
  LED3 = LED - 5mm [color="Red (633nm)" package="5 mm [THT]"]
  LED4 = LED - 5mm [color="Red (633nm)" package="5 mm [THT]"]
  LED5 = LED - 5mm [color="Red (633nm)" package="5 mm [THT]"]
  R1 = Resistor [tolerance=±5% resistance=220 package=THT]
  R2 = Resistor [tolerance=±5% resistance=220 package=THT]
  R3 = Resistor [tolerance=±5% resistance=220 package=THT]
  R4 = Resistor [tolerance=±5% resistance=220 package=THT]
  R5 = Resistor [tolerance=±5% resistance=220 package=THT]
  R6 = Resistor [tolerance=±5% resistance=220 package=THT]
  R7 = Resistor [tolerance=±5% resistance=220 package=THT]
  R8 = Resistor [tolerance=±5% resistance=220 package=THT]
  R9 = Resistor [tolerance=±5% resistance=220 package=THT]
  R10 = Resistor [tolerance=±5% resistance=220 package=THT]

nets:
  N1: Port_D2_=_LED1_Port_D11_=_LED10.D8, LED7.anode
  N2: Port_D2_=_LED1_Port_D11_=_LED10.D9_PWM, LED8.anode
  N3: Port_D2_=_LED1_Port_D11_=_LED10.D10_PWM/SS, LED9.anode
  N4: Port_D2_=_LED1_Port_D11_=_LED10.D11_PWM/MOSI, LED10.anode
  N5: Port_D2_=_LED1_Port_D11_=_LED10.GND, R3.Pin_1, R4.Pin_1, R6.Pin_1, R7.Pin_1, R8.Pin_0, R9.Pin_0
  N6: Port_D2_=_LED1_Port_D11_=_LED10.D2, LED1.cathode
  N7: Port_D2_=_LED1_Port_D11_=_LED10.D3_PWM, LED2.cathode
  N8: Port_D2_=_LED1_Port_D11_=_LED10.D4, LED3.cathode
  N9: Port_D2_=_LED1_Port_D11_=_LED10.D5_PWM, LED4.cathode
  N10: Port_D2_=_LED1_Port_D11_=_LED10.D6_PWM, LED5.cathode
  N11: Port_D2_=_LED1_Port_D11_=_LED10.D7, LED_6.cathode
  N12: LED1.anode, R4.Pin_0
  N13: LED10.cathode, R10.Pin_1
  N14: LED2.anode, R5.Pin_0
  N15: LED9.cathode, R9.Pin_1
  N16: LED8.cathode, R8.Pin_1
  N17: LED7.cathode, R1.Pin_0
  N18: LED_6.anode, R3.Pin_0
  N19: LED3.anode, R6.Pin_0
  N20: LED4.anode, R7.Pin_0
  N21: LED5.anode, R2.Pin_0
