# Fritzing sketch Pulse_Detector (saved by Fritzing 0.9.3b)
breadboards: 2

parts:
  IC1 = LM324 [package=dil16]
  P1 = S1133 Si Photodiode [package="8mm Ceramic [THT]"]
  R1 = Resistor [tolerance=±5% resistance=39k package="1206 [SMD]"]
  Composant1 = Arduino Uno (Rev3)
  C1 = Electrolytic Capacitor [capacitance=1µF package="100 mil [THT, electrolytic]"]
  R2 = Resistor [tolerance=±5% resistance=68k package=THT]
  R3 = Resistor [tolerance=±5% resistance=8.2k package=THT]
  C2 = Ceramic Capacitor [capacitance=100nF package="100 mil [THT, multilayer]"]
  C3 = Electrolytic Capacitor [capacitance=1µF package="100 mil [THT, electrolytic]"]
  R4 = Resistor [tolerance=±5% resistance=68k package=THT]
  C4 = Ceramic Capacitor [capacitance=100nF package="100 mil [THT, multilayer]"]
  R5 = Resistor [tolerance=±5% resistance=470k package=THT]
  R6 = Resistor [tolerance=±5% resistance=1.8k package=THT]
  U1 = TRANSISTOR_NPN_2 [package=to-92]
  R7 = Resistor [tolerance=±5% resistance=220 package=THT]
  LED1 = LED - 5mm [color="Red (633nm)" package="5 mm [THT]"]

nets:
  N1: IC1.OUT1, C2.1, C3.-
  N2: IC1.IN1-, R3.Pin_1, C2.0
  N3: IC1.IN1+, C1.+, R2.Pin_1
  N4: IC1.V+, R1.Pin_0, Composant1.5V, U1.E, R7.Pin_1
  GND: IC1.GND, P1.cathode, Composant1.GND, R2.Pin_0, R3.Pin_0, R4.Pin_0, LED1.cathode
  N5: IC1.IN4+, C3.+, R4.Pin_1
  N6: IC1.IN4-, C4.1, R5.Pin_1
  N7: IC1.OUT4, C4.0, R5.Pin_0, R6.Pin_1
  N8: P1.anode, R1.Pin_1, C1.-
  N9: Composant1.A0, U1.C
  N10: R6.Pin_0, U1.B
  N11: R7.Pin_0, LED1.anode

custom parts:
  LM324: LM324 Quad OpAmp
